# Fritzing sketch Sketch (saved by Fritzing 0.9.3b)
breadboards: 1

parts:
  hc-sr1 = hc-sr04
  Componente1 = Arduino Uno (Rev3)
  R1 = Resistor [tolerance=±5% resistance=220 package=THT]
  LED1 = LED - 5mm [color="Red (633nm)" package="5 mm [THT]"]

nets:
  VCC: hc-sr1.VCC, Componente1.5V
  N1: hc-sr1.Trig, Componente1.D13/SCK
  N2: hc-sr1.Echo, Componente1.D12/MISO
  GND: hc-sr1.GND, Componente1.GND, R1.Pin_0
  N3: Componente1.D2, LED1.anode
  N4: R1.Pin_1, LED1.cathode
