# Fritzing sketch supermaquina (saved by Fritzing 0.9.3b)
circuit board: 6.88079cm x 5.33095cm
breadboards: 1

parts:
  LED1 = LED - 5mm [color="Red (633nm)" package="5 mm [THT]"]
  R1 = Resistor [tolerance=±0.5% resistance=220 package=THT]
  Componente1 = Arduino Uno (Rev3)

nets:
  N1: LED1.cathode, R1.Pin_0
  N2: LED1.anode, Componente1.D13/SCK
  N3: R1.Pin_1, Componente1.GND

// code stored in the sketch: aula2_supermaquina.ino
/**
   Sequencial de leds(supermaquina effect)
   @author - Guilherme
*/
void setup() {
  //define o pino 13 como saida
  pinMode(13, OUTPUT);
}

void loop() {
  //mandar 5v no pino 13 
  digitalWrite(13, HIGH);
  //digitalWrite(13, LOW);
}

// code stored in the sketch: aula2_supermaquina2.ino

